# Fritzing sketch Aquaponik (saved by Fritzing 0.9.3b)
breadboards: 1

parts:
  U1 = NodeMCU V1.0
  Q1 = TRANSISTOR_NPN [package=to-92-ammo]
  YL-1 = YL-38 Humitidy Sensor
  Pumpe = DC Motor

nets:
  N1: U1.D1, Q1.B
  N2: U1.D4, YL-1.DIGITAL
  3V3: U1.3V3, YL-1.VCC
  GND: U1.GND, YL-1.GND, Pumpe.pin_2
  N3: U1.RSV, Q1.C
  N4: U1.A0, YL-1.ANALOG
  N5: Q1.E, Pumpe.pin_1

custom parts:
  NodeMCU V1.0: ESP8266 based NodeMCU
